# Fritzing sketch adafruit-pro-trinket-5v-circuit-diagram (saved by Fritzing 0.8.3b)
breadboards: 1

parts:
  Part1 = Pro Trinket 5V
  MIC1 = MAX4466 Electret Microphone Breakout Board
  NEOPIXEL1 = Neopixel Strip -- Black (60/m)

nets:
  N1: Part1.VBAT, NEOPIXEL1.DI
  GND: Part1.GND, MIC1.GND, NEOPIXEL1.GND
  +5V: Part1.+5V, Part1.AREF, MIC1.VCC
  N2: Part1.D6, NEOPIXEL1.+5V
  N3: Part1.A3, MIC1.out

custom parts:
  Pro Trinket 5V: The Pro Trinket 5V is like an Arduino Pro Mini with more pins and USB included. Built with the common core Arduino chip, the ATmega328p, it has 18 GPIO, 2 extra analog inputs, 28K of flash, and 2K of RAM. It has onboard USB bootloading support with Optiboot support, so you can either program your Pro Trinket over USB or with a FTDI cable. The Pro Trinket is programmable using the Arduino IDE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
  MAX4466 Electret Microphone Breakout Board: MAX4466 Electrec Microphone Breakout Board
  Neopixel Strip -- Black (60/m): Neopixel Strip, Black, 60 pixels per meter.
