# Fritzing sketch tps61169-with-pro-trinket (saved by Fritzing 0.9.3b)

parts:
  Adafruit_TPS61169_Constant_Current_Boost_Converter_LED_Driver1 = Adafruit TPS61169 Constant Current Boost Converter LED Driver [part_number=#6354]
  Part1 = Adafruit Pro Trinket 3.3V 12MHz [part_number="Adafruit #2010"]
  Part2 = Adafruit Pro Trinket LiIon/LiPoly Backpack [part_number="Adafruit #2124"]
  LED1 = LED - 3mm [color="Red (633nm)" package="3 mm [THT]"]
  LED2 = LED - 3mm [color="Red (633nm)" package="3 mm [THT]"]
  LED3 = LED - 3mm [color="Red (633nm)" package="3 mm [THT]"]
  POT1 = Breadboard Trimpot
  U1 = LIPO-2000mAh [package=lipo-2000]  # not connected

nets:
  N1: Adafruit_TPS61169_Constant_Current_Boost_Converter_LED_Driver1.PWM, Part1.D9
  N2: Adafruit_TPS61169_Constant_Current_Boost_Converter_LED_Driver1.LEDK, LED1.cathode
  N3: Adafruit_TPS61169_Constant_Current_Boost_Converter_LED_Driver1.+24V, LED3.anode
  N4: Part1.VBAT, Part2.VBAT
  GND: Part1.GND, Part2.GND
  N5: Part1.VBUS, Part2.VBUS
  N6: Part1.A0, POT1.PIN2
  N7: LED1.anode, LED2.cathode
  N8: LED2.anode, LED3.cathode

custom parts:
  Adafruit TPS61169 Constant Current Boost Converter LED Driver: The Adafruit Constant Current Boost Converter for LEDs makes driving LEDs easy, whether they're in series or parallel - with a chip that can generate up to 40V and 400mA from 3~5V input. Unlike most of our booster chips that generate a fixed voltage (like 5V, or 12V) the TPS61169 increases the voltage until a set current is being drawn. That makes it excellent for LEDs, that are specified in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
  Adafruit Pro Trinket 3.3V 12MHz: rinket's got a big sister in town - the Pro Trinket 3V! Pro Trinket combines everything you love about Trinket with the familiarity of the core Arduino chip, the ATmega328. It's like an Arduino Pro Mini with more pins and USB tossed in. Trinket's a year old now, and while its been great to see tons of tiny projects, sometimes you just need more pins, more FLASH, and more RAM. That's why we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
  Adafruit Pro Trinket LiIon/LiPoly Backpack: If you have a Pro Trinket you probably know it's the perfect little size for a portable project. This LiPoly backpack makes it really easy to do! Instead of wiring 2 or 3 boards together to make a charging system, this little PCB sits on top of the Pro Trinket and allows a LiPoly/LiIon battery to plug in. When the Pro Trinket USB port is powered, the battery is recharged automatically. Unplug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
