# Fritzing sketch Neopixel-Painter-Sketch (saved by Fritzing 0.9.2b)
breadboards: 1

parts:
  Part1 = USB Mini-B Breakout [part_number=1764]
  NEOPIXEL1 = Neopixel Strip -- White (60/m) [part_number=1138]
  Part2 = Arduino Uno (Rev3) - ICSP
  S1 = Pushbutton [package="[SMD]"]
  POT1 = Breadboard Trimpot

nets:
  GND: Part1.GND, NEOPIXEL1.GND, Part2.GND, POT1.PIN1
  5V: Part1.5V, NEOPIXEL1.+5V
  N1: NEOPIXEL1.DI, Part2.D6_PWM
  N2: Part2.A0, POT1.PIN2
  N3: Part2.A1, S1.Pin_3, S1.Pin_4
  N4: Part2.5V, POT1.PIN3

custom parts:
  USB Mini-B Breakout: Simple but effective - this breakout board has a USB Mini-B connector, with all 5 pins broken out. Great for pairing with a microcontroller with USB support, or adding USB 5V power to a project.
  Neopixel Strip -- White (60/m): Neopixel Strip, White, 60 pixels per meter.
