# Fritzing sketch wiring-diagram (saved by Fritzing 0.9.3b)
breadboards: 1

parts:
  Part1 = Adafruit Trinket 3V [part_number="Adafruit #1500"]
  S1 = Momentary Switch [package=ksa_sealed_tac_switch]
  NEOPIXEL1 = Neopixel Strip -- Black (30/m) [part_number=1376]

nets:
  GND: Part1.GND, S1.4, NEOPIXEL1.GND
  N1: Part1.#4, NEOPIXEL1.Din
  N2: Part1.VBUS, NEOPIXEL1.+5V
  N3: Part1.#1, S1.2

custom parts:
  Adafruit Trinket 3V: Trinket may be small, but do not be fooled by its size! It's a tiny microcontroller board, built around the Atmel ATtiny85, a little chip with a lot of power. We wanted to design a microcontroller board that was small enough to fit into any project, and low cost enough to use without hesitation. Perfect for when you don't want to give up your expensive dev-board and you aren't willing to take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
  Neopixel Strip -- Black (30/m): These NeoPixel strips have 30 digitally-addressable pixel LEDs per meter and are very affordable and are only 12.5 mm wide, 10 mm if you remove the strip from the casing.
