# Fritzing sketch pro-trinket-5v-hookup (saved by Fritzing 0.9.2b)
breadboards: 1

parts:
  Part1 = Adafruit TB6612 DC and Stepper Motor Driver [part_number="Adafruit #2448"]
  Part2 = Adafruit Pro Trinket 5V 16MHz [part_number="Adafruit #2000"]
  M1 = DC Motor

nets:
  VCC: Part1.PWRIN, Part1.VCC, Part1.PWMA, Part2.+5V
  GND: Part1.GND, Part2.GND
  N1: Part1.AIN1, Part2.D8
  N2: Part1.AIN2, Part2.D4
  N3: Part1.MOTORA1, M1.pin_2
  N4: Part1.MOTORA2, M1.pin_1

custom parts:
  Adafruit TB6612 DC and Stepper Motor Driver: Spin two DC motors, step one bi-polar or uni-polar stepper, or fire off two solenoids with 1.2A per channel using the TB6612. These are perhaps better known as "the drivers in our assembled Adafruit Motorshield or Motor HAT." We really like these dual H-bridges, so if you want to control motors without a shield or HAT these are easy to include on any solderless breadboard or perma-proto.
  Adafruit Pro Trinket 5V 16MHz: Trinket's got a big sister in town - the Pro Trinket 5V! Pro Trinket combines everything you love about Trinket with the familiarity of the common core Arduino chip, the ATmega328. It's like an Arduino Pro Mini with more pins and USB tossed in, so delicious. Trinket's a year old now, and while its been great to see tons of tiny projects, sometimes you just need more pins, more FLASH, and more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
