# Fritzing sketch teensy-3.2-with-tft-lcd (saved by Fritzing 0.9.2b)
breadboards: 1

parts:
  Part1 = Adafruit 1.44 inch TFT Breakout [part_number="Adafruit #2088"]
  Teensy_3_1 = Teensy 3.1
  Part2 = Adafruit Pro Trinket LiIon/LiPoly Backpack [part_number="Adafruit #2124"]
  U1 = SWITCH_SPDT [package=kps-1290]

nets:
  N1: Part1.VIN, Part2.VBAT
  N2: Part1.SCK, Teensy_3_1.D13
  N3: Part1.MOSI, Teensy_3_1.D11
  N4: Part1.TFTCS, Teensy_3_1.D9
  N5: Part1.RESET, Teensy_3_1.D8
  N6: Part1.TFTDC, Teensy_3_1.D7
  N7: Teensy_3_1.VUSB, Part2.VBUS
  N8: Part2.SW2, U1.P
  N9: Part2.SW1, U1.O

notes:
  Make sure the two traces mentioned in the Adafruit guide are cut when using this circuit diagram.

custom parts:
  Adafruit 1.44 inch TFT Breakout: This lovely little display breakout is the best way to add a small, colorful and bright display to any project. Since the display uses 4-wire SPI to communicate and has its own pixel-addressable frame buffer, it can be used with every kind of microcontroller. Even a very small one with low memory and few pins available! The 1.44" display has 128x128 color pixels. Unlike the low cost "Nokia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
  Adafruit Pro Trinket LiIon/LiPoly Backpack: If you have a Pro Trinket you probably know it's the perfect little size for a portable project. This LiPoly backpack makes it really easy to do! Instead of wiring 2 or 3 boards together to make a charging system, this little PCB sits on top of the Pro Trinket and allows a LiPoly/LiIon battery to plug in. When the Pro Trinket USB port is powered, the battery is recharged automatically. Unplug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
