# Fritzing sketch wiring-diagram (saved by Fritzing 0.9.3b)

parts:
  Part1 = Trellis Monochrome Driver PCB for 4x4 Keypad and 3mm LEDs [part_number=1616]
  Part2 = Arduino Uno (Rev3)
  Part3 = 16 NeoPixel Ring [part_number=1463]

nets:
  N1: Part1.INT, Part2.A2
  VCC: Part1.VCC, Part2.5V
  GND: Part1.GND, Part2.GND, Part3.GND
  N2: Part1.SCL, Part2.A5/SCL
  N3: Part1.SDA, Part2.A4/SDA
  N4: Part2.D6_PWM, Part3.IN
  3V3: Part2.3V3, Part3.VDD

custom parts:
  Trellis Monochrome Driver PCB for 4x4 Keypad and 3mm LEDs: Trellis is an open source backlight keypad driver system. It is easy to use, works with any 3mm LEDs and eight tiles can be tiled together on a shared I2C bus. This PCB is specially made to match the Adafruit 4x4 elastomer keypad. Each Trellis PCB has 4x4 pads and 4x4 matching spots for 3mm LEDs. The circuitry on-board handles the background key-presses and LED lighting for the 4x4 tile.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
  16 NeoPixel Ring: 16 ultra bright smart LED NeoPixels are arranged in a circle with 1.75" (44.5mm) outer diameter. The rings are 'chainable' - connect the output pin of one to the input pin of another. Use only one microcontroller pin to control as many as you can chain together! Each LED is addressable as the driver chip is inside the LED. Each one has ~18mA constant current drive so the color will be very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
