# Fritzing sketch breadboard-steampunk-hat (saved by Fritzing 1.0.1rc)
breadboards: 1

parts:
  Mod1 = Raspberry Pi Pico
  S1 = Momentary Switch [package=tactile-pth]

nets:
  N1: Mod1.pin_13, Mod1.pin_42, S1.3
  N2: Mod1.pin_27, S1.2

custom parts:
  Raspberry Pi Pico: Raspberry Pi Pico. Based around the RP2040 microcontroller the Pico is a low cost microcontroller device bringing Raspberry Pi quality, cost, and easy of use to the microcontroller space. Jan 2021, Split part in to two versions: tht (this one) and SMD. This one will drill holes for a .1 in header in pcb to allow plugging in the module as well as providing pads to solder the module to the top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
