# Fritzing sketch perfboard-usb-powered-three-wire-voltmeter-smaler (saved by Fritzing 0.9.2b)
perfboards: 1

parts:
  Part1 = Adafruit Switched JST Breakout [part_number="Adafruit #1863"]  # not connected
  J1 = female pin header, 4 pins [form="♀ (female)"]
  USBTTL1 = USB TTL Serial Cable
  J2 = female pin header, 2 pins [form="♀ (female)"]  # not connected
  VM1 = Voltmeter (3 wire)
  J3 = single row smd female pin header, 3 pins [form="♀ (female)"]

nets:
  N1: J1.pin1, USBTTL1.GND
  N2: J1.pin4, VM1.Vin
  N3: VM1.VCC, J3.pin3
  N4: VM1.GND, J3.pin2

custom parts:
  Adafruit Switched JST Breakout: This switched JST connector is the best way to quickly prototype with our LiPoly batteries. We paired a genuine JST connector with a slide switch that can do up to 600mA. Both are soldered onto a breadboard-friendly breakout. There's two ground pins, one 'switched' power pin, and one pin that is always on. This is compatible with the "JST PH 2-pin" connectors we use in our battery packs..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
  Voltmeter (3 wire): Voltmeter, 3 digit LED (.56 inch) output, 3 wire (Power 3.5V to 30V, Ground, Vin) comes in several colors (red, green, orange, blue). Available from Ebay and Amazon and others, no bezel (although bezels to fit them are currently available on Ebay). The mounting ears on what you get may or may not be the same as the ones I have. Won't run on 3.3V so you would need a 5 volt source or a 3V to 5V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
