# Fritzing sketch usb-powered-three-wire-voltmeter (saved by Fritzing 0.9.2b)
circuit board: 8.46667cm x 5.64444cm
breadboards: 1

parts:
  J1_-_JST_Breakout_Connector = female pin header, 4 pins [form="♀ (female)"]
  J2_-_JST_Connector_Spacer = female pin header, 2 pins [form="♀ (female)" part_number="number 9"]
  J4_-_Voltmeter_Connection = female pin header, 3 pins [form="♀ (female)"]
  J2_-_JST_Connector_Spacer1 = female pin header, 2 pins [form="♀ (female)" part_number="number 9"]

nets:
  N1: J1_-_JST_Breakout_Connector.pin1, J4_-_Voltmeter_Connection.pin2, J2_-_JST_Connector_Spacer1.pin1
  N2: J1_-_JST_Breakout_Connector.pin2, J2_-_JST_Connector_Spacer.pin1
  N3: J1_-_JST_Breakout_Connector.pin3, J2_-_JST_Connector_Spacer.pin2
  N4: J1_-_JST_Breakout_Connector.pin4, J4_-_Voltmeter_Connection.pin3
  N5: J4_-_Voltmeter_Connection.pin1, J2_-_JST_Connector_Spacer1.pin2

// code stored in the sketch: export.ino
w
