# Fritzing sketch wiring-diagram (saved by Fritzing 0.9.3b)

parts:
  Raspberry_Pi2 = Raspberry Pi 2
  U1 = MAX7219 [package=dil24]

nets:
  3V3: Raspberry_Pi2.3v3, U1.VCC
  N1: Raspberry_Pi2.GPIO10, U1.DIN
  N2: Raspberry_Pi2.GPIO11, U1.CLK
  N3: Raspberry_Pi2.GPIO8, U1.LOAD
  GND: Raspberry_Pi2.GND, U1.GND
