# Fritzing sketch audio-input (saved by Fritzing 0.9.3b)
breadboards: 1

parts:
  MIC1 = MAX4466 Electret Microphone Breakout Board
  Part1 = Pro Trinket 5V
  Part2 = Adafruit CharliePlex Driver IS31FL3731 [part_number="Adafruit #2946"]

nets:
  N1: MIC1.out, Part2.AUDIOIN
  GND: MIC1.GND, Part1.GND, Part2.GND
  N2: MIC1.VCC, Part1.VBUS
  N3: Part1.VBAT, Part2.VCC
  N4: Part1.A4, Part2.SDA
  N5: Part1.A5, Part2.SCL

custom parts:
  MAX4466 Electret Microphone Breakout Board: MAX4466 Electrec Microphone Breakout Board
  Pro Trinket 5V: The Pro Trinket 5V is like an Arduino Pro Mini with more pins and USB included. Built with the common core Arduino chip, the ATmega328p, it has 18 GPIO, 2 extra analog inputs, 28K of flash, and 2K of RAM. It has onboard USB bootloading support with Optiboot support, so you can either program your Pro Trinket over USB or with a FTDI cable. The Pro Trinket is programmable using the Arduino IDE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
  Adafruit CharliePlex Driver IS31FL3731: The IS31FL3731 will let you get back to that classic LED matrix look, with a nice upgrade! This I2C LED driver chip has the ability to PWM each individual LED in a 16x9 grid so you can have beautiful LED lighting effects, without a lot of pin twiddling. Simply tell the chip which LED on the grid you want lit, and what brightness and it's all taken care of for you. The IS31FL3731 is a nice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
